// Logisim project ExercicioPratico01.circ as structural Verilog: 8 circuits, main circuit halfadder
module halfadder (
  input  A,
  input  B,
  output S,
  output CO
);

  xor xor_1 (S, A, B);
  and and_1 (CO, A, B);
endmodule

module fulladder (
  input  CI,
  input  A,
  input  B,
  output S,
  output CO
);

  wire halfadder_1_co, halfadder_2_co, halfadder_2_s;

  halfadder halfadder_1 (.A(CI), .B(halfadder_2_s), .S(S), .CO(halfadder_1_co));
  halfadder halfadder_2 (.A(A), .B(B), .S(halfadder_2_s), .CO(halfadder_2_co));
  or or_1 (CO, halfadder_1_co, halfadder_2_co);
endmodule

module adder4b (
  input  C0,
  input  A0,
  input  B0,
  input  A1,
  input  B1,
  input  A2,
  input  B2,
  input  A3,
  input  B3,
  output S0,
  output S1,
  output S2,
  output S3,
  output C4,
  output OVERFLOW
);

  wire fulladder_1_co, fulladder_2_co, fulladder_3_co;

  fulladder fulladder_1 (.CI(C0), .A(A0), .B(B0), .S(S0), .CO(fulladder_1_co));
  fulladder fulladder_2 (.CI(fulladder_1_co), .A(A1), .B(B1), .S(S1), .CO(fulladder_2_co));
  fulladder fulladder_3 (.CI(fulladder_2_co), .A(A2), .B(B2), .S(S2), .CO(fulladder_3_co));
  fulladder fulladder_4 (.CI(fulladder_3_co), .A(A3), .B(B3), .S(S3), .CO(C4));
  xor xor_1 (OVERFLOW, C4, fulladder_3_co);
endmodule

module adder8b (
  input  C0,
  input  A0,
  input  B0,
  input  A1,
  input  B1,
  input  A2,
  input  B2,
  input  A3,
  input  B3,
  input  A4,
  input  B4,
  input  A5,
  input  B5,
  input  A6,
  input  B6,
  input  A7,
  input  B7,
  output S0,
  output S1,
  output S2,
  output S3,
  output S4,
  output S5,
  output S6,
  output S7,
  output C8
);

  wire adder4b_1_p14;

  // adder4b adder4b_1: pin names not known; wires that end beside it: C0, A0, B0, A1, B1, A2, B2, A3, B3, S0, S1, S2, S3, adder4b_1_p14
  // adder4b adder4b_2: pin names not known; wires that end beside it: adder4b_1_p14, A4, B4, A5, B5, A6, B6, A7, B7, S4, S5, S6, S7, C8
endmodule

module somadorsubtrador (
  input  M,
  input  A0,
  input  B0,
  input  A1,
  input  B1,
  input  A2,
  input  B2,
  input  A3,
  input  B3,
  output s0,
  output s1,
  output s2,
  output s3,
  output out_14
);

  wire fulladder_1_co, fulladder_2_co, fulladder_3_co, xor_1_out, xor_2_out, xor_3_out, xor_4_out;

  xor xor_1 (xor_1_out, B0, M);
  xor xor_2 (xor_2_out, B1, M);
  xor xor_3 (xor_3_out, B2, M);
  xor xor_4 (xor_4_out, B3, M);
  fulladder fulladder_1 (.CI(M), .A(A0), .B(xor_1_out), .S(s0), .CO(fulladder_1_co));
  fulladder fulladder_2 (.CI(fulladder_1_co), .A(A1), .B(xor_2_out), .S(s1), .CO(fulladder_2_co));
  fulladder fulladder_3 (.CI(fulladder_2_co), .A(A2), .B(xor_3_out), .S(s2), .CO(fulladder_3_co));
  fulladder fulladder_4 (.CI(fulladder_3_co), .A(A3), .B(xor_4_out), .S(s3), .CO(out_14));
endmodule

module somadorCompleto (
  input  in_1,
  input  in_2,
  input  in_3,
  output out_4,
  output out_5
);

  wire and_1_out, and_2_out, xor_1_out;

  and and_1 (and_1_out, in_2, in_3);
  xor xor_1 (xor_1_out, in_2, in_3);
  xor xor_2 (out_5, and_1_out, and_2_out);
  and and_2 (and_2_out, in_1, xor_1_out);
  xor xor_3 (out_4, in_1, xor_1_out);
endmodule

module calculadora4Bits (
  input  A0,
  input  Ci,
  input  A1,
  input  A2,
  input  A3,
  input  B0,
  input  B1,
  input  B2,
  input  B3,
  output S0,
  output S1,
  output S2,
  output S3,
  output Co,
  output OVERFLOW
);

  wire decodificador_1_a, decodificador_1_b, decodificador_1_c, decodificador_1_d, decodificador_1_e,
       decodificador_1_f, decodificador_1_g, decodificador_2_a, decodificador_2_b, decodificador_2_c,
       decodificador_2_d, decodificador_2_e, decodificador_2_f, decodificador_2_g, decodificador_3_a,
       decodificador_3_b, decodificador_3_c, decodificador_3_d, decodificador_3_e, decodificador_3_f,
       decodificador_3_g;

  adder4b adder4b_1 (
    .C0(Ci), .A0(A0), .B0(B0), .A1(A1), .B1(B1), .A2(A2), .B2(B2), .A3(A3), .B3(B3), .S0(S0), .S1(S1),
    .S2(S2), .S3(S3), .C4(Co), .OVERFLOW(OVERFLOW));
  decodificador decodificador_1 (
    .A0(A3), .A1(A2), .A2(A1), .A3(A0), .a(decodificador_1_a), .b(decodificador_1_b), .c(decodificador_1_c),
    .d(decodificador_1_d), .e(decodificador_1_e), .f(decodificador_1_f), .g(decodificador_1_g));
  decodificador decodificador_2 (
    .A0(B3), .A1(B2), .A2(B1), .A3(B0), .a(decodificador_2_a), .b(decodificador_2_b), .c(decodificador_2_c),
    .d(decodificador_2_d), .e(decodificador_2_e), .f(decodificador_2_f), .g(decodificador_2_g));
  _7_Segment_Display u_7_segment_display_1 (
    .g(decodificador_1_g), .f(decodificador_1_f), .a(decodificador_1_a), .b(decodificador_1_b),
    .e(decodificador_1_e), .d(decodificador_1_d), .c(decodificador_1_c));  // open: dp
  _7_Segment_Display u_7_segment_display_2 (
    .g(decodificador_2_g), .f(decodificador_2_f), .a(decodificador_2_a), .b(decodificador_2_b),
    .e(decodificador_2_e), .d(decodificador_2_d), .c(decodificador_2_c));  // open: dp
  decodificador decodificador_3 (
    .A0(S3), .A1(S2), .A2(S1), .A3(S0), .a(decodificador_3_a), .b(decodificador_3_b), .c(decodificador_3_c),
    .d(decodificador_3_d), .e(decodificador_3_e), .f(decodificador_3_f), .g(decodificador_3_g));
  _7_Segment_Display u_7_segment_display_3 (
    .g(decodificador_3_g), .f(decodificador_3_f), .a(decodificador_3_a), .b(decodificador_3_b),
    .e(decodificador_3_e), .d(decodificador_3_d), .c(decodificador_3_c));  // open: dp
endmodule

module decodificador (
  input  A0,
  input  A1,
  input  A2,
  input  A3,
  output a,
  output b,
  output c,
  output d,
  output e,
  output f,
  output g
);

  wire and_1_out, and_2_out, and_3_out, and_4_out, and_5_out, and_6_out, and_7_out, and_8_out, and_9_out,
       and_10_out, and_11_out, and_12_out, and_13_out, and_14_out, and_15_out, and_16_out, and_17_out,
       and_18_out, and_19_out, and_20_out, and_21_out, and_22_out, and_23_out, and_24_out, and_25_out,
       and_26_out, and_27_out, and_28_out, and_29_out, and_30_out, and_31_out, and_32_out, and_33_out,
       and_34_out, and_35_out, not_1_out, not_2_out, not_3_out, not_4_out, not_5_out, not_6_out, not_7_out,
       not_8_out, not_9_out, not_10_out, not_11_out, not_12_out, not_13_out, not_14_out, not_15_out,
       not_16_out, not_17_out, not_18_out, not_19_out, not_20_out, not_21_out, not_22_out, not_23_out,
       not_24_out, not_25_out, not_26_out, not_27_out, not_28_out, not_29_out, not_30_out, not_31_out,
       not_32_out, not_33_out, not_34_out, not_35_out, not_36_out, not_37_out, not_38_out, not_39_out,
       not_40_out, not_41_out, not_42_out, not_43_out, not_44_out;

  not not_1 (not_1_out, A1);
  and and_1 (and_1_out, not_1_out, not_2_out);
  not not_2 (not_2_out, A3);
  not not_3 (not_3_out, A0);
  and and_2 (and_2_out, not_3_out, A2);
  not not_4 (not_4_out, A0);
  and and_3 (and_3_out, not_4_out, A1, A3);
  and and_4 (and_4_out, A1, A2);
  not not_5 (not_5_out, A1);
  and and_5 (and_5_out, A0, not_5_out, not_6_out);
  not not_6 (not_6_out, A2);
  and and_6 (and_6_out, A0, not_7_out);
  not not_7 (not_7_out, A3);
  not not_8 (not_8_out, A0);
  and and_7 (and_7_out, not_8_out, not_9_out);
  not not_9 (not_9_out, A1);
  not not_10 (not_10_out, A0);
  and and_8 (and_8_out, not_10_out, not_11_out, not_12_out);
  not not_11 (not_11_out, A2);
  not not_12 (not_12_out, A3);
  not not_13 (not_13_out, A1);
  and and_9 (and_9_out, not_13_out, not_14_out);
  not not_14 (not_14_out, A3);
  not not_15 (not_15_out, A0);
  and and_10 (and_10_out, not_15_out, A2, A3);
  and and_11 (and_11_out, A0, not_16_out, A3);
  not not_16 (not_16_out, A2);
  not not_17 (not_17_out, A0);
  and and_12 (and_12_out, not_17_out, not_18_out);
  not not_18 (not_18_out, A2);
  not not_19 (not_19_out, A0);
  and and_13 (and_13_out, not_19_out, A3);
  not not_20 (not_20_out, A2);
  and and_14 (and_14_out, not_20_out, A3);
  not not_21 (not_21_out, A0);
  and and_15 (and_15_out, not_21_out, A1);
  and and_16 (and_16_out, A0, not_22_out);
  not not_22 (not_22_out, A1);
  not not_23 (not_23_out, A0);
  not not_24 (not_24_out, A1);
  and and_17 (and_17_out, not_23_out, not_24_out, not_25_out);
  not not_25 (not_25_out, A3);
  not not_26 (not_26_out, A1);
  and and_18 (and_18_out, not_26_out, A2, A3);
  not not_27 (not_27_out, A2);
  and and_19 (and_19_out, A1, not_27_out, A3);
  and and_20 (and_20_out, A1, A2, not_28_out);
  not not_28 (not_28_out, A3);
  and and_21 (and_21_out, A0, not_29_out, not_30_out);
  not not_29 (not_29_out, A2);
  not not_30 (not_30_out, A3);
  not not_31 (not_31_out, A1);
  and and_22 (and_22_out, not_31_out, not_32_out);
  not not_32 (not_32_out, A3);
  and and_23 (and_23_out, A2, not_33_out);
  not not_33 (not_33_out, A3);
  and and_24 (and_24_out, A0, A2);
  and and_25 (and_25_out, A0, A1);
  not not_34 (not_34_out, A2);
  and and_26 (and_26_out, not_34_out, not_35_out);
  not not_35 (not_35_out, A3);
  not not_36 (not_36_out, A0);
  and and_27 (and_27_out, not_36_out, A1, not_37_out);
  not not_37 (not_37_out, A2);
  and and_28 (and_28_out, A1, not_38_out);
  not not_38 (not_38_out, A3);
  and and_29 (and_29_out, A0, not_39_out);
  not not_39 (not_39_out, A1);
  and and_30 (and_30_out, A0, A2);
  not not_40 (not_40_out, A1);
  and and_31 (and_31_out, not_40_out, A2);
  and and_32 (and_32_out, A2, not_41_out);
  not not_41 (not_41_out, A3);
  not not_42 (not_42_out, A0);
  and and_33 (and_33_out, not_42_out, A1, not_43_out);
  not not_43 (not_43_out, A2);
  and and_34 (and_34_out, A0, not_44_out);
  not not_44 (not_44_out, A1);
  and and_35 (and_35_out, A0, A3);
  or or_1 (b, and_7_out, and_8_out, and_9_out, and_10_out, and_11_out);
  or or_2 (c, and_12_out, and_13_out, and_14_out, and_15_out, and_16_out);
  or or_3 (d, and_17_out, and_18_out, and_19_out, and_20_out, and_21_out);
  or or_4 (e, and_22_out, and_23_out, and_24_out, and_25_out);
  or or_5 (f, and_26_out, and_27_out, and_28_out, and_29_out, and_30_out);
  or or_6 (g, and_31_out, and_32_out, and_33_out, and_34_out, and_35_out);
  or or_7 (a, and_1_out, and_2_out, and_3_out, and_4_out, and_5_out, and_6_out);
endmodule
