// Logisim project ExercicioPratico02.circ as structural Verilog: 7 circuits, main circuit MUX
module MUX (
  input  A,
  input  B,
  input  C,
  input  D,
  input  OP1,
  input  OP2,
  output S
);

  wire and_1_out, and_2_out, and_3_out, and_4_out, not_1_out, not_2_out, not_3_out, not_4_out;

  not not_1 (not_1_out, OP1);
  not not_2 (not_2_out, OP1);
  not not_3 (not_3_out, OP2);
  not not_4 (not_4_out, OP2);
  and and_1 (and_1_out, A, not_1_out, not_3_out);
  and and_2 (and_2_out, B, not_2_out, OP2);
  and and_3 (and_3_out, C, OP1, not_4_out);
  and and_4 (and_4_out, D, OP1, OP2);
  or or_1 (S, and_1_out, and_2_out, and_3_out, and_4_out);
endmodule

module adder4bits (
  input  C0,
  input  A0,
  input  B0,
  input  A1,
  input  B1,
  input  A2,
  input  B2,
  input  A3,
  input  B3,
  output S0,
  output S1,
  output S2,
  output S3,
  output C4,
  output OVERFLOW
);

  wire somadorcompleto_1_co, somadorcompleto_2_co, somadorcompleto_3_co;

  SomadorCompleto somadorcompleto_1 (.ci(C0), .a(A0), .b(B0), .co(somadorcompleto_1_co), .s(S0));
  SomadorCompleto somadorcompleto_2 (.ci(somadorcompleto_1_co), .a(A1), .b(B1), .co(somadorcompleto_2_co), .s(S1));
  SomadorCompleto somadorcompleto_3 (.ci(somadorcompleto_2_co), .a(A2), .b(B2), .co(somadorcompleto_3_co), .s(S2));
  SomadorCompleto somadorcompleto_4 (.ci(somadorcompleto_3_co), .a(A3), .b(B3), .co(C4), .s(S3));
  xor xor_1 (OVERFLOW, C4, somadorcompleto_3_co);
endmodule

module SomadorCompleto (
  input  ci,
  input  a,
  input  b,
  output s,
  output co
);

  wire and_1_out, and_2_out, xor_1_out;

  and and_1 (and_1_out, a, b);
  xor xor_1 (xor_1_out, a, b);
  xor xor_2 (co, and_1_out, and_2_out);
  and and_2 (and_2_out, ci, xor_1_out);
  xor xor_3 (s, ci, xor_1_out);
endmodule

module ULA (
  input  B_INVERT,
  input  CarryIn,
  input  OP1,
  input  OP2,
  input  a,
  input  b,
  output SAIDA,
  output CarryOut
);

  wire and_1_out, mux1bit_1_out_4, not_1_out, not_2_out, or_1_out, somadorcompleto_1_p5;

  not not_1 (not_1_out, b);
  Mux1bit mux1bit_1 (.in_1(b), .in_2(not_1_out), .out_4(mux1bit_1_out_4), .in_3(B_INVERT));
  and and_1 (and_1_out, a, mux1bit_1_out_4);
  or or_1 (or_1_out, a, mux1bit_1_out_4);
  not not_2 (not_2_out, a);
  // SomadorCompleto somadorcompleto_1: pin names not known; wires that end beside it: a, mux1bit_1_out_4, CarryIn, CarryOut, somadorcompleto_1_p5
  MUX mux_1 (.A(and_1_out), .B(or_1_out), .D(somadorcompleto_1_p5), .S(SAIDA), .OP1(OP1), .OP2(OP2), .C(not_2_out));
endmodule

module Mux1bit (
  input  in_1,
  input  in_2,
  input  in_3,
  output out_4
);

  wire and_1_out, and_2_out, not_1_out;

  not not_1 (not_1_out, in_3);
  and and_1 (and_1_out, in_1, not_1_out);
  and and_2 (and_2_out, in_2, in_3);
  or or_1 (out_4, and_1_out, and_2_out);
endmodule

module ULA4bits (
  input  B_INVERT,
  input  OP1,
  input  OP2,
  input  B3,
  input  B2,
  input  B1,
  input  B0,
  input  A3,
  input  A2,
  input  A1,
  input  A0,
  output S0,
  output S1,
  output S2,
  output S3,
  output COUT
);

  wire ula_1_carryout, ula_2_carryout, ula_3_carryout;

  ULA ula_1 (
    .a(A0), .b(B0), .B_INVERT(B_INVERT), .CarryIn(B_INVERT), .OP1(OP1), .OP2(OP2), .CarryOut(ula_1_carryout),
    .SAIDA(S0));
  ULA ula_2 (
    .a(A1), .b(B1), .B_INVERT(B_INVERT), .CarryIn(ula_1_carryout), .OP1(OP1), .OP2(OP2),
    .CarryOut(ula_2_carryout), .SAIDA(S1));
  ULA ula_3 (
    .a(A2), .b(B2), .B_INVERT(B_INVERT), .CarryIn(ula_2_carryout), .OP1(OP1), .OP2(OP2),
    .CarryOut(ula_3_carryout), .SAIDA(S2));
  ULA ula_4 (
    .a(A3), .b(B3), .B_INVERT(B_INVERT), .CarryIn(ula_3_carryout), .OP1(OP1), .OP2(OP2), .CarryOut(COUT),
    .SAIDA(S3));
endmodule

module ULA8Bits (
);

  Multiplexer #(.select(4)) multiplexer_1 ();  // open: in0, in1, in2, in3, in4, in5, in6, in7, in8, in9, in10, in11, in12, in13, in14, in15, out, sel, en
endmodule
